# Fritzing sketch bustime-display-wiring (saved by Fritzing 0.8.7b)

parts:
  CC3K1 = Adafruit CC3000 WiFi Breakout
  Part2 = Adafruit Proto Shield for Arduino Kit - v.5
  Part1 = Arduino Uno (Rev3)
  J1 = female pin header, 10 pins [form="♀ (female)"]
  R1 = PHOTOCELL [package=photocell]
  R3 = Resistor [tolerance=±5% resistance=10k package=THT]
  J4 = male pin header, 6 pins [form="♂ (male)"]
  J6 = male pin header, 8 pins [form="♂ (male)"]
  J7 = male pin header, 8 pins [form="♂ (male)"]
  J5 = male pin header, 6 pins [form="♂ (male)"]
  S1 = Pushbutton [package="[THT]"]
  J2 = single row smd male pin header, 5 pins [form="♂ (male)"]  # not connected
  J3 = single row smd male pin header, 5 pins [form="♂ (male)"]  # not connected

nets:
  N1: CC3K1.GND, J1.pin2
  N2: CC3K1.3V3, J1.pin3
  N3: CC3K1.VIN, J1.pin4
  N4: CC3K1.CLK, J1.pin5
  N5: CC3K1.MISO, J1.pin6
  N6: CC3K1.MOSI, J1.pin7
  N7: CC3K1.CS, J1.pin8
  N8: CC3K1.VBEN, J1.pin9
  N9: CC3K1.IRQ, J1.pin10
  GND: Part2.P$6#9, Part2.P$7, Part2.P$11#14, Part2.P$12, Part2.GND, Part2.1#183, Part2.P$6#185, Part2.N$83, Part1.GND, R3.Pin_0, J6.pin7, J5.pin4, J5.pin5, S1.Pin_1, S1.Pin_2
  N10: Part2.AREF, J6.pin8
  N11: Part2.D13, Part2.P$5#167, Part2.P$6#168, Part1.D13/SCK, J6.pin6
  N12: Part2.D12, Part2.P$5#181, Part2.P$6#182, Part1.D12/MISO, J6.pin5
  N13: Part2.D11, Part2.P$5#153, Part2.P$6#154, Part1.D11_PWM/MOSI, J6.pin4
  N14: Part2.D10, Part2.P$5#138, Part2.P$6#139, Part1.D10_PWM/SS, J6.pin3
  N15: Part2.D9, Part1.D9_PWM, J6.pin2
  N16: Part2.D8, Part1.D8, J6.pin1
  N17: Part2.D0, Part1.D0/RX, J7.pin1
  N18: Part2.D1, Part1.D1/TX, J7.pin2
  N19: Part2.D2, Part2.N$103, Part1.D2, J7.pin3
  N20: Part2.D3, Part2.P$5#147, Part2.P$6#148, Part1.D3_PWM, J7.pin4
  N21: Part2.D4, Part2.N$102, Part1.D4, J7.pin5
  N22: Part2.D5, Part2.P$5#144, Part2.P$6#145, Part1.D5_PWM, J7.pin6
  N23: Part2.D6, Part2.N$270, Part1.D6_PWM, J7.pin7
  N24: Part2.D7, Part1.D7, J7.pin8
  N25: Part2.+5V, Part2.1#186, Part2.P$6#188, Part2.P$2, Part2.P$8, Part2.P$9, Part2.P$11#237, Part2.N$52, R1.P$1
  N26: Part2.RESET, S1.Pin_3, S1.Pin_4
  N27: Part2.A5, Part2.1#149, Part2.P$5#150, Part2.P$6#151, R1.P$2, R3.Pin_1
  N28: Part1.A0, J4.pin1
  N29: Part1.A1, J4.pin2
  N30: Part1.A2, J4.pin3
  N31: Part1.A3, J4.pin4
  N32: Part1.RESET, J5.pin1
  N33: Part1.3V3, J5.pin2
  N34: Part1.5V, J5.pin3
  N35: Part1.VIN, J5.pin6

custom parts:
  Adafruit CC3000 WiFi Breakout: CC3000 WiFi Breakout
  Adafruit Proto Shield for Arduino Kit - v.5: Arduino prototyping shield designed by Adafruit Industries
